# Fritzing sketch board1 (saved by Fritzing 0.9.3b)

parts:
  Часть1 = Arduino Nano (Rev3.0)
  Grove1 = Grove OLED 128x96
  J1 = Power Jack [package=power_jack_slot]
  Часть2 = Real Time Clock Module - DS1307 RTC Breakout Board
  U1 = RJ45 Jack [package=rj45-8]
  Q2 = MOSFET-NCHANNEL [package=to220v]
  R2 = Resistor [tolerance=±5% resistance=220 package=THT]
  R4 = Resistor [tolerance=±5% resistance=220 package=THT]
  S5 = Pushbutton [package="[THT]"]
  S6 = Pushbutton [package="[THT]"]
  S8 = Pushbutton [package="[THT]"]
  S7 = Pushbutton [package="[THT]"]
  R3 = Resistor [tolerance=±5% resistance=10k package=THT]
  Q3 = MOSFET-NCHANNEL [package=to220v]
  R1 = Resistor [tolerance=±5% resistance=10k package=THT]
  J2 = Piezo Speaker
  U2 = RJ45 Jack [package=rj45-8]

nets:
  GND: Часть1.GND, Часть1.A3, Часть1.A2, Часть1.A1, Часть1.A0, Grove1.GND, J1.GNDBREAK, Часть2.GND, U1.6, Q2.S, S5.Pin_3, S5.Pin_4, S6.Pin_3, S6.Pin_4, S8.Pin_3, S8.Pin_4, S7.Pin_3, S7.Pin_4, R3.Pin_1, Q3.S, R1.Pin_1, J2.pin1, U2.6
  N1: Часть1.D2, U1.1
  N2: Часть1.D3, U1.2
  N3: Часть1.D4, U1.4
  N4: Часть1.D5, R4.Pin_0
  N5: Часть1.D6, R2.Pin_0
  N6: Часть1.D7, U1.5
  N7: Часть1.D8, U2.4
  N8: Часть1.D10, J2.pin2
  N9: Часть1.D12/MISO, U2.5
  N10: Часть1.VIN, J1.PWR, U1.3, U2.3
  5V: Часть1.5V, Grove1.VCC, Часть2.5V
  N11: Часть1.A5, Grove1.SCL, Часть2.SCL
  N12: Часть1.A4, Grove1.SDA, Часть2.SDA
  N13: U1.7, Q3.D
  N14: U1.8, Q2.D
  N15: Q2.G, R4.Pin_1, R3.Pin_0
  N16: R2.Pin_1, Q3.G, R1.Pin_0
